// Logisim project MiniCpu.circ as structural Verilog: 1 circuit, main circuit main
module main (
  output [7:0] out_1,
  output [7:0] RegData2,
  output [7:0] out_3,
  output [7:0] ALUout
);

  wire and_1_out, and_2_out, and_3_out, and_4_out, and_6_out, clock_1_out, d_ff_1_q, decoder_1_out0,
       decoder_1_out1, decoder_1_out2, decoder_1_out3, not_1_out, not_2_out;
  wire [0:0] and_5_out;
  wire [3:0] multiplexer_5_out, multiplexer_5_out_2;
  wire [7:0] adder_1_out, adder_2_out, PC_q, ram_1_dout, ram_2_dout, subtractor_1_out, X0_q, X1_q, X2_q, X3_q;

  D_Flip_Flop d_ff_1 (.D(1'b1), .clk(clock_1_out), .Q(d_ff_1_q));  // open: Qn, preset, reset
  not not_1 (not_1_out, and_6_out);
  Clock clock_1 (.out(clock_1_out));
  Decoder #(.select(2)) decoder_1 (
    .out0(decoder_1_out0), .out1(decoder_1_out1), .out2(decoder_1_out2), .out3(decoder_1_out3),
    .sel(ram_1_dout[5:4]), .en(d_ff_1_q));
  Register PC (.D(adder_1_out), .clk(clock_1_out), .Q(PC_q));  // open: en, clr
  Adder adder_1 (.a(PC_q), .b(8'h1), .out(adder_1_out));  // open: cin, cout
  Hex_Digit_Display hex_digit_display_1 (.value(PC_q[7:4]));  // open: dp
  RAM ram_1 (.addr(PC_q), .we(1'b0), .oe(1'b1), .clk(clock_1_out), .dout(ram_1_dout));  // open: din
  and and_1 (and_1_out, not_1_out, decoder_1_out0);
  and and_2 (and_2_out, not_1_out, decoder_1_out1);
  and and_3 (and_3_out, not_1_out, decoder_1_out2);
  and and_4 (and_4_out, not_1_out, decoder_1_out3);
  RAM #(.asyncread("true")) ram_2 (
    .addr(ALUout), .we(and_6_out), .oe(1'b1), .clk(clock_1_out), .din(out_3), .dout(ram_2_dout));
  Hex_Digit_Display hex_digit_display_2 (.value(PC_q[3:0]));  // open: dp
  Register X0 (.D({multiplexer_5_out_2, multiplexer_5_out}), .en(and_1_out), .clk(clock_1_out), .Q(X0_q));  // open: clr
  Register X1 (.D({multiplexer_5_out_2, multiplexer_5_out}), .en(and_2_out), .clk(clock_1_out), .Q(X1_q));  // open: clr
  Register X2 (.D({multiplexer_5_out_2, multiplexer_5_out}), .en(and_3_out), .clk(clock_1_out), .Q(X2_q));  // open: clr
  Register X3 (.D({multiplexer_5_out_2, multiplexer_5_out}), .en(and_4_out), .clk(clock_1_out), .Q(X3_q));  // open: clr
  Adder adder_2 (.a(out_1), .b(RegData2), .out(adder_2_out));  // open: cin, cout
  Subtractor subtractor_1 (.a(out_1), .b(RegData2), .out(subtractor_1_out));  // open: bin, bout
  Multiplexer #(.select(2), .width(8)) multiplexer_1 (
    .in0(adder_2_out), .in1(subtractor_1_out), .out(ALUout), .sel({1'b0, and_5_out[0]}));  // open: in2, in3
  Multiplexer #(.select(2), .width(8)) multiplexer_2 (
    .in0(X0_q), .in1(X1_q), .in2(X2_q), .in3(X3_q), .out(out_1), .sel(ram_1_dout[3:2]));
  Multiplexer #(.select(2), .width(8)) multiplexer_3 (
    .in0(X0_q), .in1(X1_q), .in2(X2_q), .in3(X3_q), .out(RegData2), .sel(ram_1_dout[1:0]));
  Multiplexer #(.select(2), .width(8)) multiplexer_4 (
    .in0(X0_q), .in1(X1_q), .in2(X2_q), .in3(X3_q), .out(out_3), .sel(ram_1_dout[5:4]));
  Multiplexer #(.width(8)) multiplexer_5 (
    .in0(ALUout), .in1(ram_2_dout), .out({multiplexer_5_out_2, multiplexer_5_out}), .sel(ram_1_dout[7]));
  Hex_Digit_Display hex_digit_display_3 (.value(out_1[7:4]));  // open: dp
  Hex_Digit_Display hex_digit_display_4 (.value(RegData2[7:4]));  // open: dp
  Hex_Digit_Display hex_digit_display_5 (.value(ALUout[7:4]));  // open: dp
  Hex_Digit_Display hex_digit_display_6 (.value(multiplexer_5_out_2));  // open: dp
  Hex_Digit_Display hex_digit_display_7 (.value(out_1[3:0]));  // open: dp
  Hex_Digit_Display hex_digit_display_8 (.value(RegData2[3:0]));  // open: dp
  Hex_Digit_Display hex_digit_display_9 (.value(ALUout[3:0]));  // open: dp
  Hex_Digit_Display hex_digit_display_10 (.value(multiplexer_5_out));  // open: dp
  not not_2 (not_2_out, ram_1_dout[7]);
  and and_5 (and_5_out[0], not_2_out, ram_1_dout[6]);
  and and_6 (and_6_out, ram_1_dout[7], ram_1_dout[6]);

  // Notes on the sheet:
  //   WriteReg
  //   Names: Tracy Jiang, Jamie Lu
  //   Register File
  //   ALU
  //   Instruction Memory
  //   Data Memory
  //   ReadReg1
  //   ReadReg2
  //   RegData1
  //   Store
endmodule
